# Fritzing sketch Moon-Tree (saved by Fritzing 0.9.3b)

parts:
  Raspberry_Pi_1 = Raspberry Pi 3 [part_number=RPI-3-V1.2]
  ZS-042_RTC1 = ZS-042 RTC Module
  Bauteil1 = Adafruit TSL2561 [part_number="Adafruit #439"]
  DHT1 = DHT22 Humidity and Temperature Sensor

nets:
  N1: Raspberry_Pi_1.GPIO2, ZS-042_RTC1.SDA#2
  N2: Raspberry_Pi_1.GPIO3, ZS-042_RTC1.SCL#3
  N3: Raspberry_Pi_1.GPIO4, DHT1.DATA
  GND: Raspberry_Pi_1.GND, ZS-042_RTC1.GND#0, DHT1.GND
  5V: Raspberry_Pi_1.5V, ZS-042_RTC1.VCC#1, DHT1.VDD
  N4: ZS-042_RTC1.GND#6, Bauteil1.GND
  N5: ZS-042_RTC1.VCC#7, Bauteil1.VIN
  N6: ZS-042_RTC1.SDA#8, Bauteil1.SDA
  N7: ZS-042_RTC1.SCL#9, Bauteil1.SCL

custom parts:
  Adafruit TSL2561: The TSL2561 luminosity sensor is an advanced digital light sensor, ideal for use in a wide range of light situations. Compared to low cost CdS cells, this sensor is more precise, allowing for exact lux calculations and can be configured for different gain/timing ranges to detect light ranges from up to 0.1 - 40,000+ Lux on the fly. The best part of this sensor is that it contains both infrared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
